// Logisim project AluControl.circ as structural Verilog: 1 circuit, main circuit AluControlSignals
module AluControlSignals (
  input  [15:0] in_1,
  output isNotLogic,
  output IsNotShift,
  output [1:0] ShiftOp
);

  wire instruction_type_decoder_1_add, instruction_type_decoder_1_addi, instruction_type_decoder_1_nadd,
       instruction_type_decoder_1_naddi, instruction_type_decoder_1_ror_ror, instruction_type_decoder_1_seq,
       instruction_type_decoder_1_seqi, instruction_type_decoder_1_sll_sll, instruction_type_decoder_1_slt,
       instruction_type_decoder_1_slti, instruction_type_decoder_1_sra_sra,
       instruction_type_decoder_1_srl_srl;

  Instruction_Type_Decoder instruction_type_decoder_1 (
    .Instruction_Mem_Output(in_1), .ADD(instruction_type_decoder_1_add),
    .NADD(instruction_type_decoder_1_nadd), .SEQ(instruction_type_decoder_1_seq),
    .SLT(instruction_type_decoder_1_slt), .ADDI(instruction_type_decoder_1_addi),
    .NADDI(instruction_type_decoder_1_naddi), .SEQI(instruction_type_decoder_1_seqi),
    .SLTI(instruction_type_decoder_1_slti), .SLL_sll(instruction_type_decoder_1_sll_sll),
    .SRL_srl(instruction_type_decoder_1_srl_srl), .SRA_sra(instruction_type_decoder_1_sra_sra),
    .ROR_ror(instruction_type_decoder_1_ror_ror));  // open: a3, b3, imm5, f2, d3, imm11, AND_and, CAND_cand, OR_or, XOR_xor, ANDI, CANDI, ORI, XORI, BEQ, BNE, BLT, BGE, LW, SW, JALR, J, JAL, IMM
  or or_1 (isNotLogic, instruction_type_decoder_1_add, instruction_type_decoder_1_nadd, instruction_type_decoder_1_seq, instruction_type_decoder_1_slt, instruction_type_decoder_1_addi, instruction_type_decoder_1_naddi, instruction_type_decoder_1_seqi, instruction_type_decoder_1_slti);
  nor nor_1 (IsNotShift, instruction_type_decoder_1_sll_sll, instruction_type_decoder_1_srl_srl, instruction_type_decoder_1_sra_sra, instruction_type_decoder_1_ror_ror);
  Priority_Encoder #(.select(2)) priority_encoder_1 (
    .in0(instruction_type_decoder_1_sll_sll), .in1(instruction_type_decoder_1_srl_srl),
    .in2(instruction_type_decoder_1_sra_sra), .in3(instruction_type_decoder_1_ror_ror), .out(ShiftOp));  // open: gs, en_out, en_in
endmodule
