// Logisim project Instruction_Type_Decoder.circ as structural Verilog: 1 circuit, main circuit Instruction_Type_Decoder
module Instruction_Type_Decoder (
  input  [15:0] Instruction_Mem_Output,
  output [2:0] a3,
  output [2:0] b3,
  output [4:0] imm5,
  output [1:0] f2,
  output [2:0] d3,
  output [10:0] imm11,
  output AND_and,
  output CAND_cand,
  output OR_or,
  output XOR_xor,
  output ADD,
  output NADD,
  output SEQ,
  output SLT,
  output ANDI,
  output CANDI,
  output ORI,
  output XORI,
  output ADDI,
  output NADDI,
  output SEQI,
  output SLTI,
  output SLL_sll,
  output SRL_srl,
  output SRA_sra,
  output ROR_ror,
  output BEQ,
  output BNE,
  output BLT,
  output BGE,
  output LW,
  output SW,
  output JALR,
  output J,
  output JAL,
  output IMM
);

  wire decoder_1_out0, decoder_1_out1, not_1_out;
  wire [4:0] main_control_input_splitter_1_op5;

  Main_Control_Input_Splitter main_control_input_splitter_1 (
    .in_1(Instruction_Mem_Output), .a3(a3), .b3(b3), .Imm5(imm5), .f2(f2), .d3(d3), .Imm11(imm11),
    .Op5(main_control_input_splitter_1_op5));
  not not_1 (not_1_out, main_control_input_splitter_1_op5[4]);
  Decoder #(.select(4)) decoder_1 (
    .out0(decoder_1_out0), .out1(decoder_1_out1), .out4(ANDI), .out5(CANDI), .out6(ORI), .out7(XORI),
    .out8(ADDI), .out9(NADDI), .out10(SEQI), .out11(SLTI), .out12(SLL_sll), .out13(SRL_srl), .out14(SRA_sra),
    .out15(ROR_ror), .sel(main_control_input_splitter_1_op5[3:0]), .en(not_1_out));  // open: out2, out3
  Decoder #(.select(4)) decoder_2 (
    .out0(BEQ), .out1(BNE), .out2(BLT), .out3(BGE), .out4(LW), .out5(SW), .out11(JALR), .out12(J),
    .out13(JAL), .out14(IMM), .sel(main_control_input_splitter_1_op5[3:0]),
    .en(main_control_input_splitter_1_op5[4]));  // open: out6, out7, out8, out9, out10, out15
  Decoder #(.select(2)) decoder_3 (
    .out0(AND_and), .out1(CAND_cand), .out2(OR_or), .out3(XOR_xor), .sel(f2), .en(decoder_1_out0));
  Decoder #(.select(2)) decoder_4 (.out0(ADD), .out1(NADD), .out2(SEQ), .out3(SLT), .sel(f2), .en(decoder_1_out1));

  // Notes on the sheet:
  //   Op[3:0]
  //   Enable
  //   Decoder 1
  //   AND, CAND, OR, XOR
  //   ADD, NADD, SEQ, SLT
  //   ANDI
  //   CANDI
  //   ORI
  //   XORI
  //   ADDI
  //   NADDI
  //   SEQI
  //   SLTI
  //   SLL
  //   SRL
  //   SRA
  //   ROR
  //   Decoder 2
  //   BEQ
  //   BNE
  //   BLT
  //   BGE
  //   LW
  //   SW
  //   JALR
  //   J
  //   JAL
  //   IMM
endmodule
