// Logisim project Main Control.circ as structural Verilog: 1 circuit, main circuit main
module main (
  input  [15:0] in_1
);

  wire decoder_1_out0, decoder_1_out1, decoder_1_out4, decoder_1_out5, decoder_1_out6, decoder_1_out7,
       decoder_1_out8, decoder_1_out9, decoder_1_out10, decoder_1_out11, decoder_1_out12, decoder_1_out13,
       decoder_1_out14, decoder_1_out15, decoder_2_out0, decoder_2_out1, decoder_2_out2, decoder_2_out3,
       decoder_2_out4, decoder_2_out5, decoder_2_out11, decoder_2_out12, decoder_2_out13, decoder_2_out14,
       not_1_out;

  Decoder #(.select(4)) decoder_1 (
    .out0(decoder_1_out0), .out1(decoder_1_out1), .out4(decoder_1_out4), .out5(decoder_1_out5),
    .out6(decoder_1_out6), .out7(decoder_1_out7), .out8(decoder_1_out8), .out9(decoder_1_out9),
    .out10(decoder_1_out10), .out11(decoder_1_out11), .out12(decoder_1_out12), .out13(decoder_1_out13),
    .out14(decoder_1_out14), .out15(decoder_1_out15), .sel(in_1[3:0]), .en(not_1_out));  // open: out2, out3
  not not_1 (not_1_out, in_1[4]);
  Decoder #(.select(4)) decoder_2 (
    .out0(decoder_2_out0), .out1(decoder_2_out1), .out2(decoder_2_out2), .out3(decoder_2_out3),
    .out4(decoder_2_out4), .out5(decoder_2_out5), .out11(decoder_2_out11), .out12(decoder_2_out12),
    .out13(decoder_2_out13), .out14(decoder_2_out14), .sel(in_1[3:0]), .en(in_1[4]));  // open: out6, out7, out8, out9, out10, out15

  // Notes on the sheet:
  //   Imm 11
  //   5-bit Opcode
  //   a 3
  //   b 3
  //   Imm 5
  //   f 2
  //   d 3
  //   Op[3:0]
  //   Enable
  //   Decoder 1
  //   Decoder 2
  //   AND, CAND, OR, XOR
  //   ADD, NADD, SEQ, SLT
  //   ANDI
  //   CANDI
  //   ORI
  //   XORI
  //   ADDI
  //   NADDI
  //   SEQI
  //   SLTI
  //   SLL
  //   SRL
  //   SRA
  //   ROR
  //   BEQ
  //   BNE
  //   BLT
  //   BGE
  //   LW
  //   SW
  //   JALR
  //   J
  //   JAL
  //   IMM
endmodule
