// Logisim project Main_Control.circ as structural Verilog: 1 circuit, main circuit main_control
module main_control (
  input  [15:0] in_1,
  output RegDst,
  output RegWr,
  output ALUSrc,
  output WBData,
  output MemRead,
  output MemWrite
);

  wire instruction_type_decoder_1_add, instruction_type_decoder_1_addi, instruction_type_decoder_1_and_and,
       instruction_type_decoder_1_andi, instruction_type_decoder_1_cand_cand,
       instruction_type_decoder_1_candi, instruction_type_decoder_1_jalr, instruction_type_decoder_1_nadd,
       instruction_type_decoder_1_naddi, instruction_type_decoder_1_or_or, instruction_type_decoder_1_ori,
       instruction_type_decoder_1_ror_ror, instruction_type_decoder_1_seq, instruction_type_decoder_1_seqi,
       instruction_type_decoder_1_sll_sll, instruction_type_decoder_1_slt, instruction_type_decoder_1_slti,
       instruction_type_decoder_1_sra_sra, instruction_type_decoder_1_srl_srl,
       instruction_type_decoder_1_xor_xor, instruction_type_decoder_1_xori, or_2_out;

  Instruction_Type_Decoder instruction_type_decoder_1 (
    .Instruction_Mem_Output(in_1), .AND_and(instruction_type_decoder_1_and_and),
    .CAND_cand(instruction_type_decoder_1_cand_cand), .OR_or(instruction_type_decoder_1_or_or),
    .XOR_xor(instruction_type_decoder_1_xor_xor), .ADD(instruction_type_decoder_1_add),
    .NADD(instruction_type_decoder_1_nadd), .SEQ(instruction_type_decoder_1_seq),
    .SLT(instruction_type_decoder_1_slt), .ANDI(instruction_type_decoder_1_andi),
    .CANDI(instruction_type_decoder_1_candi), .ORI(instruction_type_decoder_1_ori),
    .XORI(instruction_type_decoder_1_xori), .ADDI(instruction_type_decoder_1_addi),
    .NADDI(instruction_type_decoder_1_naddi), .SEQI(instruction_type_decoder_1_seqi),
    .SLTI(instruction_type_decoder_1_slti), .SLL_sll(instruction_type_decoder_1_sll_sll),
    .SRL_srl(instruction_type_decoder_1_srl_srl), .SRA_sra(instruction_type_decoder_1_sra_sra),
    .ROR_ror(instruction_type_decoder_1_ror_ror), .LW(MemRead), .SW(MemWrite),
    .JALR(instruction_type_decoder_1_jalr));  // open: a3, b3, imm5, f2, d3, imm11, BEQ, BNE, BLT, BGE, J, JAL, IMM
  or or_1 (RegDst, instruction_type_decoder_1_and_and, instruction_type_decoder_1_cand_cand, instruction_type_decoder_1_or_or, instruction_type_decoder_1_xor_xor, instruction_type_decoder_1_add, instruction_type_decoder_1_nadd, instruction_type_decoder_1_seq, instruction_type_decoder_1_slt);
  or or_2 (or_2_out, instruction_type_decoder_1_andi, instruction_type_decoder_1_candi, instruction_type_decoder_1_ori, instruction_type_decoder_1_xori, instruction_type_decoder_1_addi, instruction_type_decoder_1_seqi, instruction_type_decoder_1_slti, instruction_type_decoder_1_sll_sll, instruction_type_decoder_1_srl_srl, instruction_type_decoder_1_sra_sra, instruction_type_decoder_1_ror_ror, MemRead, instruction_type_decoder_1_jalr);
  or or_3 (RegWr, RegDst, or_2_out);
  or or_4 (ALUSrc, instruction_type_decoder_1_andi, instruction_type_decoder_1_candi, instruction_type_decoder_1_ori, instruction_type_decoder_1_xori, instruction_type_decoder_1_addi, instruction_type_decoder_1_naddi, instruction_type_decoder_1_seqi, instruction_type_decoder_1_slti, instruction_type_decoder_1_sll_sll, instruction_type_decoder_1_srl_srl, MemRead, instruction_type_decoder_1_sra_sra, MemWrite, instruction_type_decoder_1_ror_ror);

  assign WBData = MemRead;
endmodule
