// Logisim project Main_Control_Input_Splitter.circ as structural Verilog: 1 circuit, main circuit Main_Control_Input_Splitter
module Main_Control_Input_Splitter (
  input  [15:0] in_1,
  output [2:0] a3,
  output [2:0] b3,
  output [4:0] Imm5,
  output [1:0] f2,
  output [2:0] d3,
  output [10:0] Imm11,
  output [4:0] Op5
);


  assign a3 = in_1[7:5];
  assign b3 = in_1[10:8];
  assign d3 = in_1[15:13];
  assign f2 = in_1[12:11];
  assign Imm5 = in_1[15:11];
  assign Imm11 = in_1[15:5];
  assign Op5 = in_1[4:0];

  // Notes on the sheet:
  //   a 3
  //   b 3
  //   Imm 5
  //   Imm 11
  //   5-bit Opcode
  //   f 2
  //   d 3
endmodule
