// Logisim project PC_Control_.circ as structural Verilog: 1 circuit, main circuit pc_control
module pc_control (
  input  Zero,
  input  LT,
  input  EQ,
  input  [4:0] OpCode,
  output PCSrc_0,
  output PCSrc_2,
  output PCSrc_3,
  output PCSrc_1
);

  wire and_1_out, and_2_out, and_3_out, and_4_out, comparator_1_eq, comparator_2_eq, comparator_3_eq,
       comparator_4_eq, comparator_6_eq, comparator_7_eq, not_1_out, not_2_out, or_1_out;

  not not_1 (not_1_out, Zero);
  Comparator #(.width(5)) comparator_1 (.a(OpCode), .b(5'b10000), .eq(comparator_1_eq));  // open: gt, lt
  Comparator #(.width(5)) comparator_2 (.a(OpCode), .b(5'b10001), .eq(comparator_2_eq));  // open: gt, lt
  Comparator #(.width(5)) comparator_3 (.a(OpCode), .b(5'b10010), .eq(comparator_3_eq));  // open: gt, lt
  Comparator #(.width(5)) comparator_4 (.a(OpCode), .b(5'b10011), .eq(comparator_4_eq));  // open: gt, lt
  Comparator #(.width(5)) comparator_5 (.a(OpCode), .b(5'b11011), .eq(PCSrc_3));  // open: gt, lt
  Comparator #(.width(5)) comparator_6 (.a(OpCode), .b(5'b11100), .eq(comparator_6_eq));  // open: gt, lt
  Comparator #(.width(5)) comparator_7 (.a(OpCode), .b(5'b11101), .eq(comparator_7_eq));  // open: gt, lt
  and and_1 (and_1_out, Zero, comparator_1_eq);
  and and_2 (and_2_out, not_1_out, comparator_2_eq);
  and and_3 (and_3_out, LT, comparator_3_eq);
  not not_2 (not_2_out, LT);
  or or_1 (or_1_out, not_2_out, EQ);
  and and_4 (and_4_out, or_1_out, comparator_4_eq);
  or or_2 (PCSrc_1, comparator_6_eq, comparator_7_eq);
  nor nor_1 (PCSrc_0, PCSrc_2, PCSrc_3, PCSrc_1);
  or or_3 (PCSrc_2, and_1_out, and_2_out, and_3_out, and_4_out);
endmodule
