// Logisim project datapath.circ as structural Verilog: 2 circuits, main circuit main
module main (
  input  in_1
);

  wire alu_1_out_11, alu_1_zeroflag, alucontrolsignals_1_isnotlogic, alucontrolsignals_1_isnotshift,
       clock_1_out, main_control_1_p2, main_control_1_p3, main_control_1_p4, main_control_1_p5,
       main_control_1_p6, main_control_1_p7;
  wire [1:0] alucontrolsignals_1_shiftop, mcisplit1_1_f2;
  wire [2:0] mcisplit1_1_a3, mcisplit1_1_b3, mcisplit1_1_d3, multiplexer_1_out;
  wire [4:0] mcisplit1_1_imm5, mcisplit1_1_op5;
  wire [10:0] mcisplit1_1_imm11, shifter_1_out;
  wire [15:0] rom_1_data;
  wire [19:0] adder_1_out, bit_extender_1_out, register_1_q;
  wire [31:0] alu_1_aluout, bit_extender_2_out, DataMemory_dout, multiplexer_2_out, multiplexer_3_out,
       registerfile_1_busa, registerfile_1_busb;

  pc_control pc_control_1 (
    .Zero(alu_1_zeroflag), .LT(alu_1_out_11), .EQ(alu_1_zeroflag), .OpCode(mcisplit1_1_op5));  // open: PCSrc_0, PCSrc_2, PCSrc_3, PCSrc_1
  Clock clock_1 (.out(clock_1_out));
  Register #(.width(20)) register_1 (.D(adder_1_out), .en(1'b1), .clk(clock_1_out), .Q(register_1_q), .clr(in_1));
  Adder #(.width(20)) adder_1 (.a(register_1_q), .b(20'h2), .out(adder_1_out));  // open: cin, cout
  ROM #(.addrWidth(20), .dataWidth(16)) rom_1 (.addr(register_1_q), .data(rom_1_data));
  assign bit_extender_1_out = {{9{shifter_1_out[10]}}, shifter_1_out};  // Bit_Extender bit_extender_1
  Shifter #(.width(11)) shifter_1 (.in(mcisplit1_1_imm11), .\dist (4'b0001), .out(shifter_1_out));
  mcisplit1 mcisplit1_1 (
    .Instruction(rom_1_data), .f2(mcisplit1_1_f2), .d3(mcisplit1_1_d3), .Imm5(mcisplit1_1_imm5),
    .b3(mcisplit1_1_b3), .a3(mcisplit1_1_a3), .Imm11(mcisplit1_1_imm11), .Op5(mcisplit1_1_op5));
  Multiplexer #(.width(3)) multiplexer_1 (
    .in0(mcisplit1_1_b3), .in1(mcisplit1_1_d3), .out(multiplexer_1_out), .sel(main_control_1_p2));
  // main_control main_control_1: pin names not known; wires that end beside it: rom_1_data, main_control_1_p2, main_control_1_p3, main_control_1_p4, main_control_1_p5, main_control_1_p6, main_control_1_p7
  assign bit_extender_2_out = {{27{mcisplit1_1_imm5[4]}}, mcisplit1_1_imm5};  // Bit_Extender bit_extender_2
  registerFile registerfile_1 (
    .BusW(multiplexer_3_out), .RA(mcisplit1_1_a3), .RB(mcisplit1_1_b3), .RegWrite(main_control_1_p3),
    .RW(multiplexer_1_out), .clk(clock_1_out), .BusA(registerfile_1_busa), .BusB(registerfile_1_busb));
  Multiplexer #(.width(32)) multiplexer_2 (
    .in0(registerfile_1_busb), .in1(bit_extender_2_out), .out(multiplexer_2_out), .sel(main_control_1_p4));
  AluControlSignals alucontrolsignals_1 (
    .in_1(rom_1_data), .isNotLogic(alucontrolsignals_1_isnotlogic),
    .IsNotShift(alucontrolsignals_1_isnotshift), .ShiftOp(alucontrolsignals_1_shiftop));
  ALU alu_1 (
    .BusA(registerfile_1_busa), .BusB(multiplexer_2_out), .ShiftOp(alucontrolsignals_1_shiftop),
    .IsNotShift(alucontrolsignals_1_isnotshift), .isNotLogic(alucontrolsignals_1_isnotlogic),
    .f(mcisplit1_1_f2), .AluOut(alu_1_aluout), .ZeroFlag(alu_1_zeroflag), .out_11(alu_1_out_11));  // open: in_6, in_7
  RAM #(.addrWidth(18), .dataWidth(32)) DataMemory (
    .addr(alu_1_aluout[19:2]), .we(main_control_1_p7), .oe(main_control_1_p6), .clk(clock_1_out),
    .din(registerfile_1_busb), .dout(DataMemory_dout));
  Multiplexer #(.width(32)) multiplexer_3 (
    .in0(alu_1_aluout), .in1(DataMemory_dout), .out(multiplexer_3_out), .sel(main_control_1_p5));

  // Notes on the sheet:
  //   contents of rom_1 (hex, n*v repeats v):
  //   94c 5*0 515f 0 af40
endmodule

module mcisplit1 (
  input  [15:0] Instruction,
  output [1:0] f2,
  output [2:0] d3,
  output [4:0] Imm5,
  output [2:0] b3,
  output [2:0] a3,
  output [10:0] Imm11,
  output [4:0] Op5
);


  assign a3 = Instruction[10:8];
  assign b3 = Instruction[7:5];
  assign d3 = Instruction[4:2];
  assign f2 = Instruction[1:0];
  assign Imm5 = Instruction[4:0];
  assign Imm11 = Instruction[10:0];
  assign Op5 = Instruction[15:11];
endmodule
