// Logisim project pc.circ as structural Verilog: 1 circuit, main circuit Program_Counter
module Program_Counter (
  input  in_1
);

  wire clock_1_out;
  wire [19:0] switch_1_p1, switch_1_p2, switch_1_p3;

  // Switch switch_1: pin names not known; wires that end beside it: switch_1_p1, switch_1_p2, switch_1_p3
  Register #(.width(20)) register_1 (.D(switch_1_p2), .en(1'b1), .clk(clock_1_out), .Q(switch_1_p3), .clr(in_1));
  Clock clock_1 (.out(clock_1_out));
  Adder #(.width(20)) adder_1 (.a(switch_1_p3), .b(20'h2), .out(switch_1_p1));  // open: cin, cout
endmodule
