// Logisim project registerFile.circ as structural Verilog: 1 circuit, main circuit registerFile
module registerFile (
  input  [31:0] BusW,
  input  [2:0] RA,
  input  [2:0] RB,
  input  RegWrite,
  input  [2:0] RW,
  input  clk,
  output [31:0] BusA,
  output [31:0] BusB
);

  wire decoder_1_out1, decoder_1_out2, decoder_1_out3, decoder_1_out4, decoder_1_out5, decoder_1_out6,
       decoder_1_out7, decoder_2_out0, decoder_2_out1, decoder_2_out2, decoder_2_out3, decoder_2_out4,
       decoder_2_out5, decoder_2_out6, decoder_2_out7, decoder_3_out0, decoder_3_out1, decoder_3_out2,
       decoder_3_out3, decoder_3_out4, decoder_3_out5, decoder_3_out6, decoder_3_out7;
  wire [31:0] register_1_q, register_2_q, register_3_q, register_4_q, register_5_q, register_6_q,
       register_7_q;

  Decoder #(.select(3)) decoder_1 (
    .out1(decoder_1_out1), .out2(decoder_1_out2), .out3(decoder_1_out3), .out4(decoder_1_out4),
    .out5(decoder_1_out5), .out6(decoder_1_out6), .out7(decoder_1_out7), .sel(RW), .en(RegWrite));  // open: out0
  Register #(.width(32)) register_1 (.D(BusW), .en(decoder_1_out1), .clk(clk), .Q(register_1_q));  // open: clr
  Register #(.width(32)) register_2 (.D(BusW), .en(decoder_1_out2), .clk(clk), .Q(register_2_q));  // open: clr
  Register #(.width(32)) register_3 (.D(BusW), .en(decoder_1_out3), .clk(clk), .Q(register_3_q));  // open: clr
  Register #(.width(32)) register_4 (.D(BusW), .en(decoder_1_out4), .clk(clk), .Q(register_4_q));  // open: clr
  Register #(.width(32)) register_5 (.D(BusW), .en(decoder_1_out5), .clk(clk), .Q(register_5_q));  // open: clr
  Register #(.width(32)) register_6 (.D(BusW), .en(decoder_1_out6), .clk(clk), .Q(register_6_q));  // open: clr
  Register #(.width(32)) register_7 (.D(BusW), .en(decoder_1_out7), .clk(clk), .Q(register_7_q));  // open: clr
  assign BusA = decoder_2_out0 ? {32{1'b0}} : 32'bz;  // Controlled_Buffer controlled_buffer_1
  Decoder #(.enable("false"), .select(3)) decoder_2 (
    .out0(decoder_2_out0), .out1(decoder_2_out1), .out2(decoder_2_out2), .out3(decoder_2_out3),
    .out4(decoder_2_out4), .out5(decoder_2_out5), .out6(decoder_2_out6), .out7(decoder_2_out7), .sel(RA));
  assign BusA = decoder_2_out1 ? register_1_q : 32'bz;  // Controlled_Buffer controlled_buffer_2
  assign BusA = decoder_2_out2 ? register_2_q : 32'bz;  // Controlled_Buffer controlled_buffer_3
  assign BusA = decoder_2_out3 ? register_3_q : 32'bz;  // Controlled_Buffer controlled_buffer_4
  assign BusA = decoder_2_out4 ? register_4_q : 32'bz;  // Controlled_Buffer controlled_buffer_5
  assign BusA = decoder_2_out5 ? register_5_q : 32'bz;  // Controlled_Buffer controlled_buffer_6
  assign BusA = decoder_2_out6 ? register_6_q : 32'bz;  // Controlled_Buffer controlled_buffer_7
  assign BusA = decoder_2_out7 ? register_7_q : 32'bz;  // Controlled_Buffer controlled_buffer_8
  assign BusB = decoder_3_out0 ? {32{1'b0}} : 32'bz;  // Controlled_Buffer controlled_buffer_9
  Decoder #(.enable("false"), .select(3)) decoder_3 (
    .out0(decoder_3_out0), .out1(decoder_3_out1), .out2(decoder_3_out2), .out3(decoder_3_out3),
    .out4(decoder_3_out4), .out5(decoder_3_out5), .out6(decoder_3_out6), .out7(decoder_3_out7), .sel(RB));
  assign BusB = decoder_3_out1 ? register_1_q : 32'bz;  // Controlled_Buffer controlled_buffer_10
  assign BusB = decoder_3_out2 ? register_2_q : 32'bz;  // Controlled_Buffer controlled_buffer_11
  assign BusB = decoder_3_out3 ? register_3_q : 32'bz;  // Controlled_Buffer controlled_buffer_12
  assign BusB = decoder_3_out4 ? register_4_q : 32'bz;  // Controlled_Buffer controlled_buffer_13
  assign BusB = decoder_3_out5 ? register_5_q : 32'bz;  // Controlled_Buffer controlled_buffer_14
  assign BusB = decoder_3_out6 ? register_6_q : 32'bz;  // Controlled_Buffer controlled_buffer_15
  assign BusB = decoder_3_out7 ? register_7_q : 32'bz;  // Controlled_Buffer controlled_buffer_16
endmodule
