// Logisim project shifter_unit.circ as structural Verilog: 1 circuit, main circuit my_shifter
module my_shifter (
  input  [31:0] BusA,
  input  [31:0] Imm,
  input  [1:0] in_3,
  output [31:0] ShiftOut
);

  wire [31:0] shifter_1_out, shifter_2_out, shifter_3_out, shifter_4_out;

  Shifter #(.width(32)) shifter_1 (.in(BusA), .\dist (Imm[4:0]), .out(shifter_1_out));
  Shifter #(.shift("lr"), .width(32)) shifter_2 (.in(BusA), .\dist (Imm[4:0]), .out(shifter_2_out));
  Shifter #(.shift("ar"), .width(32)) shifter_3 (.in(BusA), .\dist (Imm[4:0]), .out(shifter_3_out));
  Shifter #(.shift("rr"), .width(32)) shifter_4 (.in(BusA), .\dist (Imm[4:0]), .out(shifter_4_out));
  Multiplexer #(.select(2), .width(32)) multiplexer_1 (
    .in0(shifter_1_out), .in1(shifter_2_out), .in2(shifter_3_out), .in3(shifter_4_out), .out(ShiftOut),
    .sel(in_3));
endmodule
